// Logisim project onetotwo.circ as structural Verilog: 3 circuits, main circuit onebitnc
module onebitnc (
  input  A,
  input  B,
  output S,
  output C
);

  Adder #(.width(1)) adder_1 (.a(A), .b(B), .out(S), .cout(C));  // open: cin
endmodule

module twobitnc (
  input  [1:0] in_1,
  input  [1:0] in_2,
  output [1:0] S,
  output C
);

  wire onebitnc_1_c, onebitnc_2_c, onebitnc_2_s, onebitwc_1_out_3, onebitwc_1_out_4;

  onebitnc onebitnc_1 (.A(in_1[0]), .B(in_2[0]), .S(S[0]), .C(onebitnc_1_c));
  onebitnc onebitnc_2 (.A(in_1[1]), .B(in_2[1]), .S(onebitnc_2_s), .C(onebitnc_2_c));
  onebitwc onebitwc_1 (.in_1(in_1[1]), .in_2(in_2[1]), .out_3(onebitwc_1_out_3), .out_4(onebitwc_1_out_4));
  Multiplexer #(.enable("false")) multiplexer_1 (
    .in0(onebitnc_2_s), .in1(onebitwc_1_out_3), .out(S[1]), .sel(onebitnc_1_c));
  Multiplexer #(.enable("false")) multiplexer_2 (
    .in0(onebitnc_2_c), .in1(onebitwc_1_out_4), .out(C), .sel(onebitnc_1_c));
endmodule

module onebitwc (
  input  in_1,
  input  in_2,
  output out_3,
  output out_4
);

  Adder #(.width(1)) adder_1 (.a(in_1), .b(in_2), .out(out_3), .cin(1'b1), .cout(out_4));
endmodule
